// Digital circuit ex3.dig as structural Verilog
module ex3 (
  input  [1:0] A,
  input  [1:0] B,
  output Y
);

  wire A0_t, A1_t, and_1_out, and_2_out, and_3_out, and_4_out, and_5_out, B0_t, B1_t, or_1_out;

  not not_1 (A0_t, A[0]);
  not not_2 (A1_t, A[1]);
  not not_3 (B0_t, B[0]);
  not not_4 (B1_t, B[1]);
  and and_1 (and_1_out, A[1], B[1]);
  and and_2 (and_2_out, A1_t, B1_t);
  and and_3 (and_3_out, A[0], B0_t);
  and and_4 (and_4_out, A[1], B1_t);
  or or_1 (or_1_out, and_1_out, and_2_out);
  and and_5 (and_5_out, or_1_out, and_3_out);
  or or_2 (Y, and_4_out, and_5_out);
endmodule

/* Test case EX3 Test:
A B Y 

 0b00 0b00 0
 0b00 0b01 0
 0b00 0b10 0
 0b00 0b11 0
 0b01 0b00 1
 0b01 0b01 0
 0b01 0b10 0
 0b01 0b11 0
 0b10 0b00 1
 0b10 0b01 1
 0b10 0b10 0
 0b10 0b11 0
 0b11 0b00 1
 0b11 0b01 1
 0b11 0b10 1
 0b11 0b11 0
*/
