// Digital circuit comparator.dig as structural Verilog
module comparator (
  input  Sign,
  input  Overflow,
  output Result
);

  xor xor_1 (Result, Sign, Overflow);
endmodule

/* Test case Comparator Test:
Sign Overflow Result
0 0 0
0 1 1
1 0 1
1 1 0
*/
