// Digital circuit control-unit.dig as structural Verilog
module control_unit (
  input  [6:0] opcode,
  input  [2:0] funct3,
  input  [6:0] funct7,
  output RegWrite,
  output ImmSrc1,
  output ImmSrc0,
  output ALUOp3,
  output ALUOp2,
  output ALUOp1,
  output ALUOp0,
  output [7:0] Result,
  output ALUSrc
);

  wire Add, And, and_1_out, and_2_out, and_3_out, and_4_out, and_9_out, and_10_out, and_11_out, and_12_out,
       comparator_3_eq, comparator_4_eq, comparator_5_eq, comparator_6_eq, comparator_7_eq, comparator_8_eq,
       comparator_9_eq, comparator_10_eq, comparator_11_eq, comparator_12_eq, comparator_13_eq,
       comparator_14_eq, comparator_15_eq, comparator_16_eq, comparator_17_eq, comparator_18_eq,
       comparator_19_eq, comparator_20_eq, comparator_21_eq, isAdd, isAddi, isAnd, isAndi, isOr, isRType,
       isSll, isSlt, isSlti, isSra, isSrl, isSub, Slt;
  wire [2:0] priorityencoder_1_num;

  Comparator #(.Bits(7)) comparator_1 (.a(opcode), .b(7'b0110011), .eq(isRType));  // open: gt, lt
  Comparator #(.Bits(7)) comparator_2 (.a(opcode), .b(7'b0010011), .eq(ALUSrc));  // open: gt, lt
  Comparator #(.Bits(3)) comparator_3 (.a(funct3), .b(3'b000), .eq(comparator_3_eq));  // open: gt, lt
  Comparator #(.Bits(7)) comparator_4 (.a(funct7), .b({7{1'b0}}), .eq(comparator_4_eq));  // open: gt, lt
  Comparator #(.Bits(3)) comparator_5 (.a(funct3), .b(3'b000), .eq(comparator_5_eq));  // open: gt, lt
  Comparator #(.Bits(7)) comparator_6 (.a(funct7), .b(7'b0100000), .eq(comparator_6_eq));  // open: gt, lt
  Comparator #(.Bits(3)) comparator_7 (.a(funct3), .b(3'b010), .eq(comparator_7_eq));  // open: gt, lt
  Comparator #(.Bits(7)) comparator_8 (.a(funct7), .b({7{1'b0}}), .eq(comparator_8_eq));  // open: gt, lt
  Comparator #(.Bits(3)) comparator_9 (.a(funct3), .b(3'b101), .eq(comparator_9_eq));  // open: gt, lt
  Comparator #(.Bits(7)) comparator_10 (.a(funct7), .b({7{1'b0}}), .eq(comparator_10_eq));  // open: gt, lt
  and and_1 (and_1_out, comparator_3_eq, comparator_4_eq);
  and and_2 (and_2_out, comparator_5_eq, comparator_6_eq);
  and and_3 (and_3_out, comparator_7_eq, comparator_8_eq);
  and and_4 (and_4_out, comparator_9_eq, comparator_10_eq);
  and and_5 (isAdd, and_1_out, isRType);
  and and_6 (isSub, and_2_out, isRType);
  and and_7 (isSlt, and_3_out, isRType);
  and and_8 (isSrl, and_4_out, isRType);
  Comparator #(.Bits(3)) comparator_11 (.a(funct3), .b(3'b111), .eq(comparator_11_eq));  // open: gt, lt
  Comparator #(.Bits(7)) comparator_12 (.a(funct7), .b({7{1'b0}}), .eq(comparator_12_eq));  // open: gt, lt
  Comparator #(.Bits(3)) comparator_13 (.a(funct3), .b(3'b110), .eq(comparator_13_eq));  // open: gt, lt
  Comparator #(.Bits(7)) comparator_14 (.a(funct7), .b({7{1'b0}}), .eq(comparator_14_eq));  // open: gt, lt
  Comparator #(.Bits(3)) comparator_15 (.a(funct3), .b(3'b001), .eq(comparator_15_eq));  // open: gt, lt
  Comparator #(.Bits(7)) comparator_16 (.a(funct7), .b({7{1'b0}}), .eq(comparator_16_eq));  // open: gt, lt
  Comparator #(.Bits(3)) comparator_17 (.a(funct3), .b(3'b101), .eq(comparator_17_eq));  // open: gt, lt
  Comparator #(.Bits(7)) comparator_18 (.a(funct7), .b(7'b0100000), .eq(comparator_18_eq));  // open: gt, lt
  and and_9 (and_9_out, comparator_11_eq, comparator_12_eq);
  and and_10 (and_10_out, comparator_13_eq, comparator_14_eq);
  and and_11 (and_11_out, comparator_15_eq, comparator_16_eq);
  and and_12 (and_12_out, comparator_17_eq, comparator_18_eq);
  and and_13 (isAnd, and_9_out, isRType);
  and and_14 (isOr, and_10_out, isRType);
  and and_15 (isSll, and_11_out, isRType);
  and and_16 (isSra, and_12_out, isRType);
  PriorityEncoder #(.Selector_Bits(3)) priorityencoder_1 (
    .in0(Add), .in1(isSub), .in2(And), .in3(isOr), .in4(Slt), .in5(isSll), .in6(isSrl), .in7(isSra),
    .num(priorityencoder_1_num));  // open: any
  Comparator #(.Bits(3)) comparator_19 (.a(funct3), .b(3'b000), .eq(comparator_19_eq));  // open: gt, lt
  Comparator #(.Bits(3)) comparator_20 (.a(funct3), .b(3'b010), .eq(comparator_20_eq));  // open: gt, lt
  Comparator #(.Bits(3)) comparator_21 (.a(funct3), .b(3'b111), .eq(comparator_21_eq));  // open: gt, lt
  and and_17 (isAddi, comparator_19_eq, ALUSrc);
  and and_18 (isSlti, comparator_20_eq, ALUSrc);
  and and_19 (isAndi, comparator_21_eq, ALUSrc);
  ROM #(.AddrBits(3), .Bits(8)) rom_1 (
    .A(priorityencoder_1_num), .sel(1'b1),
    .D({RegWrite, Result[6], ImmSrc1, ImmSrc0, ALUOp3, ALUOp2, ALUOp1, ALUOp0}));
  or or_1 (Add, isAdd, isAddi);
  or or_2 (And, isAnd, isAndi);
  or or_3 (Slt, isSlt, isSlti);

  assign {Result[7], Result[5:0]} = {RegWrite, ImmSrc1, ImmSrc0, ALUOp3, ALUOp2, ALUOp1, ALUOp0};

  // Other names for the same wires on the sheet: f3[2:0] = funct3; f7[6:0] = funct7; isIType = ALUSrc;
  //   OPC[6:0] = opcode

  // Notes on the sheet:
  //   OPCode Logic
  //   Input
  //   RType
  //   isAdd Logic
  //   isSub Logic
  //   isSlt Logic
  //   isSrl Logic
  //   isAnd Logic
  //   isOr Logic
  //   isSll Logic
  //   isSra Logic
  //   IType
  //   isAddi Logic
  //   isSlti Logic
  //   isAndi Logic
  //   contents of rom_1 (hex, n*v repeats v):
  //   82,86,80,81,87,84,85,88
  //   Second Logic
  //   Add?
  //   And?
endmodule

/* Test case:
opcode funct3 funct7 Result RegWrite ALUSrc ImmSrc1 ImmSrc0 ALUOp3 ALUOp2 ALUOp1 ALUOp0
# ADD Test
0b0110011 0b000 0b0000000 0b10000010 1 0 0 0 0 0 1 0
# SUB Test
0b0110011 0b000 0b0100000 0b10000110 1 0 0 0 0 1 1 0
# AND Test
0b0110011 0b111 0b0000000 0b10000000 1 0 0 0 0 0 0 0
# OR Test
0b0110011 0b110 0b0000000 0b10000001 1 0 0 0 0 0 0 1
# SLT Test
0b0110011 0b010 0b0000000 0b10000111 1 0 0 0 0 1 1 1
# SLL Test
0b0110011 0b001 0b0000000 0b10000100 1 0 0 0 0 1 0 0
# SRL Test
0b0110011 0b101 0b0000000 0b10000101 1 0 0 0 0 1 0 1
# SRA Test
0b0110011 0b101 0b0100000 0b10001000 1 0 0 0 1 0 0 0
*/
