// Digital circuit cpu.dig as structural Verilog
module cpu (
  input  clk,
  output [31:0] ReadData1,
  output [31:0] ReadData2
);

  wire ALUSrc, RegWrite;
  wire [2:0] f3;
  wire [3:0] control_unit_1_aluop3;
  wire [4:0] ReadReg1, ReadReg2, WriteReg;
  wire [6:0] f7, opcode;
  wire [31:0] add_1_s, Immediate, multiplexer_1_out, PC_q, Result;

  Register #(.Bits(32), .isProgramCounter("true")) PC (.D(add_1_s), .C(clk), .en(1'b1), .Q(PC_q));
  Add #(.Bits(32)) add_1 (.a(32'h4), .b(PC_q), .c_i(1'b0), .s(add_1_s));  // open: c_o
  ROM #(.AddrBits(10), .isProgramMemory("true"), .Bits(32)) Instruction_Memory (
    .A(PC_q[11:2]), .sel(1'b1), .D({f7, ReadReg2, ReadReg1, f3, WriteReg, opcode}));
  register_file register_file_1 (
    .ReadReg1(ReadReg1), .ReadReg2(ReadReg2), .WriteReg(WriteReg), .WriteData(Result), .RegWrite(RegWrite),
    .Clock(clk), .ReadData1(ReadData1), .ReadData2(ReadData2));
  control_unit control_unit_1 (
    .opcode(opcode), .funct3(f3), .funct7(f7), .RegWrite(RegWrite), .ALUOp3(control_unit_1_aluop3[3]),
    .ALUOp2(control_unit_1_aluop3[2]), .ALUOp1(control_unit_1_aluop3[1]), .ALUOp0(control_unit_1_aluop3[0]),
    .ALUSrc(ALUSrc));  // open: ImmSrc1, ImmSrc0, Result
  BitExtender #(.inputBits(12), .outputBits(32)) bitextender_1 (.in({f7, ReadReg2}), .out(Immediate));
  Multiplexer #(.Bits(32)) multiplexer_1 (.sel(ALUSrc), .in_0(ReadData2), .in_1(Immediate), .out(multiplexer_1_out));
  alu alu_1 (.A(ReadData1), .B(multiplexer_1_out), .ALUOp(control_unit_1_aluop3), .Result(Result));  // open: FlagZ

  // Other names for the same wires on the sheet: clock = clk; rd1[31:0] = ReadData1; rd2[31:0] = ReadData2

  // Notes on the sheet:
  //   contents of Instruction_Memory (hex, n*v repeats v):
  //   fec00213,7f020293,70128313,53130393,12337713,71c77793,54178893
  //   ,13722913,292993,92a13,ffda2a93,5aab13,b0013,fec22b93,b8013,fa65ac13
  //   ,c0013,22c93,c8013,2585ad13,d0013,fff22d93,d8013,520433,6404b3
  //   ,40448533,40750533,526633,6666b3,737833,587e33,522eb3,42af33,521433
  //   ,4314b3,42d533,5355b3,40525633,404356b3
endmodule

/* Test case cpu:
clk ReadData1 ReadData2
0 0 0        # addi x4, x0, -20
C (-20) 0    # addi x5, x4, 0x7F0      ; x4 = -20
C 2012 0     # addi x6, x5, 0x701      ; x5 = 2012
C 3805 0     # addi x7, x6, 0x531      ; x6 = 3805
C 3805 0     # andi x14, x6, 0x123     ; rs1 = x6
C 1 0        # andi x15, x14, 0x71C    ; rs1 = x14 = 1
C 0 0        # andi x17, x15, 0x541    ; rs1 = x15 = 0
C (-20) 0    # slti x18, x4, 311       ; rs1 = x4
C 1 0        # slti x19, x18, 2        ; rs1 = x18 = 1
C 1 0        # slti x20, x19, 0        ; rs1 = x19 = 1
C 0 0        # slti x21, x20, -3       ; rs1 = x20 = 0
C 0 2012     # slti x22, x21, 5        ; rs1 = x21 = 0
C 1 0        # addi x0,  x22, 0        ; rs1 = x22 = 1 (write to x0 ignored)
C (-20) 0    # slti x23, x4,  -20      ; rs1 = x4
C 0 0        # addi x0,  x23, 0        ; rs1 = x23 = 0
C 0 3805     # slti x24, x11, -90      ; x11 was never set, so 0
C 0 0        # addi x0,  x24, 0        ; rs1 = x24 = 0
C (-20) 0    # slti x25, x4,  0        ; rs1 = x4
C 1 0        # addi x0,  x25, 0        ; rs1 = x25 = 1
C 0 0        # slti x26, x11, 600      ; x11 still 0
C 1 0        # addi x0,  x26, 0        ; rs1 = x26 = 1
C (-20) 0    # slti x27, x4,  -1       ; rs1 = x4
C 1 0        # addi x0,  x27, 0        ; rs1 = x27 = 1
C (-20) 0x7DC  # add x8, x4, x5   ; reads x4=-20, x5=7DC
C 0x7C8 0xEDD    # add x9, x8, x6   ; reads x8=7C8, x6=EDD
C 0x16A5 0xFFFFFFEC # sub x10, x9, x4 ; reads x9=16A5, x4=-20
C 0x16B9 0x140E  # sub x11, x10, x7 ; reads x10=16B9, x7=140E
C (-20) 2012 # or x12, x4, x5          ; rs1 = x4, rs2 = x5
C (-4) 3805  # or x13, x12, x6         ; rs1 = x12, rs2 = x6
C 3805 5134  # and x16, x6, x7         ; rs1 = x6, rs2 = x7
C 1036 2012  # and x28, x16, x5        ; rs1 = x16, rs2 = x5
C (-20) 2012 # slt x29, x4, x5         ; rs1 = x4, rs2 = x5
C 2012 (-20) # slt x30, x5, x4         ; rs1 = x5, rs2 = x4
C (-20) 2012 # sll x8, x4, x5          ; rs1 = x4, rs2 = x5
C 3805 (-20) # sll x9, x6, x4          ; rs1 = x6, rs2 = x4
C 2012 (-20) # srl x10, x5, x4         ; rs1 = x5, rs2 = x4
C 3805 2012  # srl x11, x6, x5         ; rs1 = x6, rs2 = x5
C (-20) 2012 # sra x12, x4, x5         ; rs1 = x4, rs2 = x5
C 3805 (-20) # sra x13, x6, x4         ; rs1 = x6, rs2 = x4
*/
