// Digital circuit register-file.dig as structural Verilog
module register_file (
  input  [4:0] ReadReg1,
  input  [4:0] ReadReg2,
  input  [4:0] WriteReg,
  input  [31:0] WriteData,
  input  RegWrite,
  input  Clock,
  output [31:0] ReadData1,
  output [31:0] ReadData2
);

  wire and_1_out, and_2_out, and_3_out, and_4_out, and_5_out, and_6_out, and_7_out, and_8_out, and_9_out,
       and_10_out, and_11_out, and_12_out, and_13_out, and_14_out, and_15_out, and_16_out, and_17_out,
       and_18_out, and_19_out, and_20_out, and_21_out, and_22_out, and_23_out, and_24_out, and_25_out,
       and_26_out, and_27_out, and_28_out, and_29_out, and_30_out, and_31_out, r_1_t, r_2_t, r_3, r_4, r_5,
       r_6, r_7, r_8, r_9, r_10, r_11, r_12, r_13, r_14, r_15, r_16, r_17, r_18, r_19, r_20, r_21, r_22,
       r_23, r_24, r_25, r_26, r_27, r_28, r_29, r_30, r_31;
  wire [31:0] rq_1, rq_2, rq_3, rq_4, rq_5, rq_6, rq_7, rq_8, rq_9, rq_10, rq_11, rq_12, rq_13, rq_14, rq_15,
       rq_16, rq_17, rq_18, rq_19, rq_20, rq_21, rq_22, rq_23, rq_24, rq_25, rq_26, rq_27, rq_28, rq_29,
       rq_30, rq_31;

  Multiplexer #(.Selector_Bits(5), .Bits(32)) multiplexer_1 (
    .sel(ReadReg1), .in_0({32{1'b0}}), .in_1(rq_1), .in_2(rq_2), .in_3(rq_3), .in_4(rq_4), .in_5(rq_5),
    .in_6(rq_6), .in_7(rq_7), .in_8(rq_8), .in_9(rq_9), .in_10(rq_10), .in_11(rq_11), .in_12(rq_12),
    .in_13(rq_13), .in_14(rq_14), .in_15(rq_15), .in_16(rq_16), .in_17(rq_17), .in_18(rq_18), .in_19(rq_19),
    .in_20(rq_20), .in_21(rq_21), .in_22(rq_22), .in_23(rq_23), .in_24(rq_24), .in_25(rq_25), .in_26(rq_26),
    .in_27(rq_27), .in_28(rq_28), .in_29(rq_29), .in_30(rq_30), .in_31(rq_31), .out(ReadData1));
  Multiplexer #(.Selector_Bits(5), .Bits(32)) multiplexer_2 (
    .sel(ReadReg2), .in_0({32{1'b0}}), .in_1(rq_1), .in_2(rq_2), .in_3(rq_3), .in_4(rq_4), .in_5(rq_5),
    .in_6(rq_6), .in_7(rq_7), .in_8(rq_8), .in_9(rq_9), .in_10(rq_10), .in_11(rq_11), .in_12(rq_12),
    .in_13(rq_13), .in_14(rq_14), .in_15(rq_15), .in_16(rq_16), .in_17(rq_17), .in_18(rq_18), .in_19(rq_19),
    .in_20(rq_20), .in_21(rq_21), .in_22(rq_22), .in_23(rq_23), .in_24(rq_24), .in_25(rq_25), .in_26(rq_26),
    .in_27(rq_27), .in_28(rq_28), .in_29(rq_29), .in_30(rq_30), .in_31(rq_31), .out(ReadData2));
  Decoder #(.Selector_Bits(5)) decoder_1 (
    .sel(WriteReg), .out_1(r_1_t), .out_2(r_2_t), .out_3(r_3), .out_4(r_4), .out_5(r_5), .out_6(r_6),
    .out_7(r_7), .out_8(r_8), .out_9(r_9), .out_10(r_10), .out_11(r_11), .out_12(r_12), .out_13(r_13),
    .out_14(r_14), .out_15(r_15), .out_16(r_16), .out_17(r_17), .out_18(r_18), .out_19(r_19), .out_20(r_20),
    .out_21(r_21), .out_22(r_22), .out_23(r_23), .out_24(r_24), .out_25(r_25), .out_26(r_26), .out_27(r_27),
    .out_28(r_28), .out_29(r_29), .out_30(r_30), .out_31(r_31));  // open: out_0
  and and_1 (and_1_out, r_1_t, RegWrite);
  and and_2 (and_2_out, r_2_t, RegWrite);
  and and_3 (and_3_out, r_3, RegWrite);
  and and_4 (and_4_out, r_4, RegWrite);
  and and_5 (and_5_out, r_5, RegWrite);
  and and_6 (and_6_out, r_6, RegWrite);
  Register #(.Bits(32)) R1 (.D(WriteData), .C(Clock), .en(and_1_out), .Q(rq_1));
  Register #(.Bits(32)) R2 (.D(WriteData), .C(Clock), .en(and_2_out), .Q(rq_2));
  Register #(.Bits(32)) R3 (.D(WriteData), .C(Clock), .en(and_3_out), .Q(rq_3));
  Register #(.Bits(32)) R4 (.D(WriteData), .C(Clock), .en(and_4_out), .Q(rq_4));
  Register #(.Bits(32)) R5 (.D(WriteData), .C(Clock), .en(and_5_out), .Q(rq_5));
  Register #(.Bits(32)) R6 (.D(WriteData), .C(Clock), .en(and_6_out), .Q(rq_6));
  and and_7 (and_7_out, r_7, RegWrite);
  and and_8 (and_8_out, r_8, RegWrite);
  and and_9 (and_9_out, r_9, RegWrite);
  and and_10 (and_10_out, r_10, RegWrite);
  and and_11 (and_11_out, r_11, RegWrite);
  and and_12 (and_12_out, r_12, RegWrite);
  Register #(.Bits(32)) R7 (.D(WriteData), .C(Clock), .en(and_7_out), .Q(rq_7));
  Register #(.Bits(32)) R8 (.D(WriteData), .C(Clock), .en(and_8_out), .Q(rq_8));
  Register #(.Bits(32)) R9 (.D(WriteData), .C(Clock), .en(and_9_out), .Q(rq_9));
  Register #(.Bits(32)) R10 (.D(WriteData), .C(Clock), .en(and_10_out), .Q(rq_10));
  Register #(.Bits(32)) R11 (.D(WriteData), .C(Clock), .en(and_11_out), .Q(rq_11));
  Register #(.Bits(32)) R12 (.D(WriteData), .C(Clock), .en(and_12_out), .Q(rq_12));
  and and_13 (and_13_out, r_13, RegWrite);
  and and_14 (and_14_out, r_14, RegWrite);
  and and_15 (and_15_out, r_15, RegWrite);
  and and_16 (and_16_out, r_16, RegWrite);
  and and_17 (and_17_out, r_17, RegWrite);
  and and_18 (and_18_out, r_18, RegWrite);
  Register #(.Bits(32)) R13 (.D(WriteData), .C(Clock), .en(and_13_out), .Q(rq_13));
  Register #(.Bits(32)) R14 (.D(WriteData), .C(Clock), .en(and_14_out), .Q(rq_14));
  Register #(.Bits(32)) R15 (.D(WriteData), .C(Clock), .en(and_15_out), .Q(rq_15));
  Register #(.Bits(32)) R16 (.D(WriteData), .C(Clock), .en(and_16_out), .Q(rq_16));
  Register #(.Bits(32)) R17 (.D(WriteData), .C(Clock), .en(and_17_out), .Q(rq_17));
  Register #(.Bits(32)) R18 (.D(WriteData), .C(Clock), .en(and_18_out), .Q(rq_18));
  and and_19 (and_19_out, r_19, RegWrite);
  and and_20 (and_20_out, r_20, RegWrite);
  and and_21 (and_21_out, r_21, RegWrite);
  and and_22 (and_22_out, r_22, RegWrite);
  and and_23 (and_23_out, r_23, RegWrite);
  and and_24 (and_24_out, r_24, RegWrite);
  Register #(.Bits(32)) R19 (.D(WriteData), .C(Clock), .en(and_19_out), .Q(rq_19));
  Register #(.Bits(32)) R20 (.D(WriteData), .C(Clock), .en(and_20_out), .Q(rq_20));
  Register #(.Bits(32)) R21 (.D(WriteData), .C(Clock), .en(and_21_out), .Q(rq_21));
  Register #(.Bits(32)) R22 (.D(WriteData), .C(Clock), .en(and_22_out), .Q(rq_22));
  Register #(.Bits(32)) R23 (.D(WriteData), .C(Clock), .en(and_23_out), .Q(rq_23));
  Register #(.Bits(32)) R24 (.D(WriteData), .C(Clock), .en(and_24_out), .Q(rq_24));
  and and_25 (and_25_out, r_25, RegWrite);
  and and_26 (and_26_out, r_26, RegWrite);
  and and_27 (and_27_out, r_27, RegWrite);
  and and_28 (and_28_out, r_28, RegWrite);
  and and_29 (and_29_out, r_29, RegWrite);
  and and_30 (and_30_out, r_30, RegWrite);
  Register #(.Bits(32)) R25 (.D(WriteData), .C(Clock), .en(and_25_out), .Q(rq_25));
  Register #(.Bits(32)) R26 (.D(WriteData), .C(Clock), .en(and_26_out), .Q(rq_26));
  Register #(.Bits(32)) R27 (.D(WriteData), .C(Clock), .en(and_27_out), .Q(rq_27));
  Register #(.Bits(32)) R28 (.D(WriteData), .C(Clock), .en(and_28_out), .Q(rq_28));
  Register #(.Bits(32)) R29 (.D(WriteData), .C(Clock), .en(and_29_out), .Q(rq_29));
  Register #(.Bits(32)) R30 (.D(WriteData), .C(Clock), .en(and_30_out), .Q(rq_30));
  and and_31 (and_31_out, r_31, RegWrite);
  Register #(.Bits(32)) R31 (.D(WriteData), .C(Clock), .en(and_31_out), .Q(rq_31));

  // Other names for the same wires on the sheet: C = Clock; R_1[4:0] = ReadReg1; R_2[4:0] = ReadReg2;
  //   RD_1[31:0] = ReadData1; RD_2[31:0] = ReadData2
endmodule

/* Test case Register File Test:
WriteReg WriteData RegWrite Clock ReadReg1 ReadReg2 ReadData1 ReadData2

# $1 = 25
1 25 1 C 1 0 25 0

# $2 = 30
2 30 1 C 0 2 0 30

# $(N+1) = (N+1)
loop(N, 30)
	(N+1) (N+1) 1 C (N+1) (N) (N+1) (N)
end loop

# $(N+1) = N-60
loop(N, 30)
	(N+1) (N-60) 1 C (N+1) (N+1) (N-60) (N-60)
end loop

# Try writing to $0. This should not write anything
0 25 1 C 0 0 0 0

# try writing when RegWrite = 0
# (the registers should still have their old values)
loop(N, 30)
	(N+1) (N+80) 0 C (N+1) (N+1) (N-60) (N-60)
end loop
*/
